// Logisim project Project3Given.circ as structural Verilog: 10 circuits, main circuit CPU15
module main (
  input  EnableBreakpoint,
  input  [14:0] Breakpoint
);

  wire and_2_out, and_3_out, chipset_1_irq, CLK, clock_1_out, cpu15_1_c, cpu15_1_e, cpu15_1_i, cpu15_1_n,
       cpu15_1_o, cpu15_1_z, KBCLR, KBIRQ, KBRD, MEMCS, nand_1_out, RE, TTYCLR, TTYWE, WE;
  wire [6:0] KBDATA, TTYDATA;
  wire [7:0] cpu15_1_srf;
  wire [14:0] ADDR, chipset_1_ivect, chipset_1_led0, chipset_1_led1, chipset_1_led2, chipset_1_led3,
       chipset_1_led4, chipset_1_led5, chipset_1_led6, chipset_1_led7, chipset_1_led8, chipset_1_led9,
       chipset_1_leda, chipset_1_ledb, chipset_1_ledc, chipset_1_ledd, chipset_1_lede, cpu15_1_ib,
       cpu15_1_pc, cpu15_1_r0, cpu15_1_r1, cpu15_1_r2, cpu15_1_r3, cpu15_1_r4, cpu15_1_r5, cpu15_1_r6,
       cpu15_1_r7, cpu15_1_srp, DATA, xnor_1_out;

  Clock clock_1 (.out(clock_1_out));
  nand nand_1 (nand_1_out, EnableBreakpoint, xnor_1_out[0], xnor_1_out[1], xnor_1_out[2], xnor_1_out[3], xnor_1_out[4], xnor_1_out[5], xnor_1_out[6], xnor_1_out[7], xnor_1_out[8], xnor_1_out[9], xnor_1_out[10], xnor_1_out[11], xnor_1_out[12], xnor_1_out[13], xnor_1_out[14], 1'b1);
  and and_1 (CLK, clock_1_out, nand_1_out);
  assign xnor_1_out = ~(Breakpoint ^ cpu15_1_pc);  // XNOR_Gate xnor_1, 15 bits wide
  LED I (.in(cpu15_1_i));
  LED Z (.in(cpu15_1_z));
  LED N (.in(cpu15_1_n));
  LED O (.in(cpu15_1_o));
  LED C (.in(cpu15_1_c));
  LED E (.in(cpu15_1_e));
  and and_2 (and_2_out, WE, MEMCS);
  and and_3 (and_3_out, MEMCS, RE);
  RAM #(.addrWidth(15), .asyncread("true"), .dataWidth(15), .databus("bidir")) ram_1 (
    .addr(ADDR), .we(and_2_out), .oe(and_3_out), .clk(CLK), .data(DATA));
  // Probe on cpu15_1_pc
  // Probe on cpu15_1_ib
  // Probe on cpu15_1_srp
  // Probe on cpu15_1_srf
  // Probe on cpu15_1_r0
  // Probe on cpu15_1_r1
  // Probe on cpu15_1_r2
  // Probe on cpu15_1_r3
  // Probe on cpu15_1_r4
  // Probe on cpu15_1_r5
  // Probe on cpu15_1_r6
  // Probe on cpu15_1_r7
  CPU15 cpu15_1 (
    .I(cpu15_1_i), .Z(cpu15_1_z), .N(cpu15_1_n), .O(cpu15_1_o), .C(cpu15_1_c), .E(cpu15_1_e),
    .PC(cpu15_1_pc), .IB(cpu15_1_ib), .SRP(cpu15_1_srp), .SRF(cpu15_1_srf), .R0(cpu15_1_r0), .R1(cpu15_1_r1),
    .R2(cpu15_1_r2), .R3(cpu15_1_r3), .R4(cpu15_1_r4), .R5(cpu15_1_r5), .R6(cpu15_1_r6), .R7(cpu15_1_r7),
    .CLK(CLK), .IRQ(chipset_1_irq), .RE(RE), .WE(WE), .ADDR(ADDR), .DATAIN(DATA), .DATAOUT(DATA));
  // Probe on ADDR
  // Probe on DATA
  // Probe on chipset_1_ivect
  // Probe on TTYDATA
  CHIPSET chipset_1 (
    .RE(RE), .WE(WE), .ADDR(ADDR), .CPUDATAIN(DATA), .CPUDATAOUT(DATA), .IRQ(chipset_1_irq),
    .IVECT(chipset_1_ivect), .CLK(CLK), .MEMCS(MEMCS), .TTYWR(TTYWE), .TTYCLR(TTYCLR), .TTYDATA(TTYDATA),
    .KBRD(KBRD), .KBCLR(KBCLR), .KBIRQ(KBIRQ), .KBDATA(KBDATA), .LED0(chipset_1_led0), .LED1(chipset_1_led1),
    .LED2(chipset_1_led2), .LED3(chipset_1_led3), .LED4(chipset_1_led4), .LED5(chipset_1_led5),
    .LED6(chipset_1_led6), .LED7(chipset_1_led7), .LED8(chipset_1_led8), .LED9(chipset_1_led9),
    .LEDA(chipset_1_leda), .LEDB(chipset_1_ledb), .LEDC(chipset_1_ledc), .LEDD(chipset_1_ledd),
    .LEDE(chipset_1_lede));
  TTY tty_1 (.data(TTYDATA), .clk(CLK), .we(TTYWE), .clr(TTYCLR));
  Keyboard keyboard_1 (.clk(CLK), .re(KBRD), .clr(KBCLR), .avail(KBIRQ), .data(KBDATA));
  DotMatrix #(.matrixcols(15), .matrixrows(15)) dotmatrix_1 (
    .col0(chipset_1_led0), .col1(chipset_1_led1), .col2(chipset_1_led2), .col3(chipset_1_led3),
    .col4(chipset_1_led4), .col5(chipset_1_led5), .col6(chipset_1_led6), .col7(chipset_1_led7),
    .col8(chipset_1_led8), .col9(chipset_1_led9), .col10(chipset_1_leda), .col11(chipset_1_ledb),
    .col12(chipset_1_ledc), .col13(chipset_1_ledd), .col14(chipset_1_lede));
endmodule

// CPU
module CPU15 (
  input  [14:0] DATAIN,
  input  CLK,
  input  IRQ,
  output [14:0] PC,
  output [14:0] IB,
  output [14:0] SRP,
  output [7:0] SRF,
  output [14:0] R0,
  output [14:0] R1,
  output [14:0] R2,
  output [14:0] R3,
  output [14:0] R4,
  output [14:0] R5,
  output [14:0] R6,
  output [14:0] R7,
  output RE,
  output WE,
  output I,
  output Z,
  output [14:0] ADDR,
  output N,
  output O,
  output C,
  output E,
  output [14:0] DATAOUT
);

  wire Load, regw, SRFW, SRPW, Store, SWI, undriven;
  wire [1:0] Asel, Bsel, flagsrc;
  wire [2:0] ALUop, regd;
  wire [7:0] flagWM;
  wire [14:0] IM_data, immB, regs15_1_a, regs15_1_b;

  RAM #(.addrWidth(15), .dataWidth(15)) ram_1 (.addr(ADDR), .we(Store), .oe(undriven));  // open: clk, din, dout
  Counter #(.max('h7fff), .width(15)) pcc (.clk(CLK), .Q(PC));  // open: clr, load, up, count, D, carry
  Controlled_Buffer #(.width(15)) controlled_buffer_1 ();  // open: in, out, en
  ROM #(.addrWidth(15), .dataWidth(15)) IM (.addr(PC), .data(IM_data));
  IMM15 imm15_1 (.INST(IM_data), .SEXT(immB));
  Register #(.width(15)) register_1 (.D(IM_data), .en(1'b1), .Q(ADDR), .clk(CLK));  // open: clr
  REGS15 regs15_1 (
    .D(ADDR), .W(regw), .SelD(regd), .CLK(CLK), .SelA(ADDR[10:8]), .SelB(ADDR[13:11]), .R0(R0), .R1(R1),
    .R2(R2), .R3(R3), .R4(R4), .R5(R5), .R6(R6), .R7(R7), .A(regs15_1_a), .B(regs15_1_b));
  ALU15 alu15_1 (.A(regs15_1_a), .B(immB), .OP(ALUop), .CIN(C), .OIN(O), .R(DATAOUT), .C(C), .O(O), .N(N), .Z(Z));
  DECODE15 decode15_1 (
    .OPCODE(ADDR[4:0]), .SWI(SWI), .STORE(Store), .LOAD(Load), .ASEL(Asel), .BSEL(Bsel), .ALUOP(ALUop),
    .REGDATASRC(regd), .REGW(regw), .FLAGSRC(flagsrc), .FLAGWM(flagWM), .SRPW(SRPW), .SRFW(SRFW));

  assign IB = ADDR;

  // Other names for the same wires on the sheet: OPcode[4:0] = ADDR[4:0]; DATA[14:0] = DATAIN; SelA[2:0] = ADDR[10:8];
  //   SelB[2:0] = ADDR[13:11]

  // Notes on the sheet:
  //   contents of IM (hex, n*v repeats v):
  //   1d90 1150 6a64 313 29a2 481 58de 6164 34b7 19cb 4c2e 36d2 51 6c81 14ea 7374 1032 5e19 2c6e 5746 2b99
  //   1a5 5ada 6564 34b0 5d19 240e 6616 63ab 15cc 149a 4149 271d 80e 6408 56e7 2393 6481 60de 696e 3a10
  //   1d1b 640e 726 7b3b 4985 5a14 2020 1010 1312 240f 312 6102 1105 2882 a20 1010 813 ae4 783 1161 c0
  //   50f0 3129 510 808 409 4572 3c1 4cb0 4062 2878 1894 4288 404 204 62b9 1e0 6858 2032 143c c4a 2144 202
  //   102 315c 40f0 352c 1019 4a1e 625 10a2 101 81 1c9e 500a 1010 808 9c9 7500 5101 80 409c 4f50 522 1055
  //   827 20a2 101 81 882 5420 183c c0d 708 30a2 101 81 882 5420 183c c4d 2728 40a2 101 81 882 5420 183c
  //   c8d 4828 50a2 101 81 882 5420 183c ccd 6848 60a0
endmodule

module CHIPSET (
  input  RE,
  input  WE,
  input  [14:0] ADDR,
  input  [14:0] CPUDATAIN,
  input  KBIRQ,
  input  [6:0] KBDATA,
  input  CLK,
  output MEMCS,
  output TTYWR,
  output [14:0] IVECT,
  output TTYCLR,
  output [6:0] TTYDATA,
  output KBRD,
  output KBCLR,
  output [14:0] CPUDATAOUT,
  output IRQ,
  output [14:0] LED0,
  output [14:0] LED1,
  output [14:0] LED2,
  output [14:0] LED3,
  output [14:0] LED4,
  output [14:0] LED5,
  output [14:0] LED6,
  output [14:0] LED7,
  output [14:0] LED8,
  output [14:0] LED9,
  output [14:0] LEDA,
  output [14:0] LEDB,
  output [14:0] LEDC,
  output [14:0] LEDD,
  output [14:0] LEDE
);

  wire and_1_out, and_8_out, and_10_out, DATA7, IOCS, IVECTADDR, IVECTEN, IVECTRE, KBCS, LED0EN, LED0END,
       LED1EN, LED1END, LED2EN, LED2END, LED3EN, LED3END, LED4EN, LED4END, LED5EN, LED5END, LED6EN, LED6END,
       LED7EN, LED7END, LED8EN, LED8END, LED9EN, LED9END, LEDAEN, LEDAEND, LEDBEN, LEDBEND, LEDCEN, LEDCEND,
       LEDCS, LEDDEN, LEDDEND, LEDEEN, LEDEEND, LEDFEND, LEDRE, multiplexer_17_out, multiplexer_18_out, RWE,
       TTYCS;
  wire [14:0] DATAL0, DATAL1, DATAL2, DATAL3, DATAL4, DATAL5, DATAL6, DATAL7, DATAL8, DATAL9, DATALA, DATALB,
       DATALC, DATALD, DATALE, LEDDATA;
  wire [14:8] KBDATA15;

  assign CPUDATAOUT = KBRD ? {KBDATA15, DATA7, KBDATA} : 15'bz;  // Controlled_Buffer controlled_buffer_1
  assign CPUDATAOUT = LEDRE ? LEDDATA : 15'bz;  // Controlled_Buffer controlled_buffer_2
  assign CPUDATAOUT = IVECTRE ? IVECT : 15'bz;  // Controlled_Buffer controlled_buffer_3
  Register #(.width(15)) register_1 (.D(DATAL0), .en(LED0EN), .Q(LED0), .clk(CLK));  // open: clr
  Register #(.width(15)) register_2 (.D(DATAL1), .en(LED1EN), .Q(LED1), .clk(CLK));  // open: clr
  Register #(.width(15)) register_3 (.D(DATAL2), .en(LED2EN), .Q(LED2), .clk(CLK));  // open: clr
  Register #(.width(15)) register_4 (.D(DATAL3), .en(LED3EN), .Q(LED3), .clk(CLK));  // open: clr
  Register #(.width(15)) register_5 (.D(DATAL4), .en(LED4EN), .Q(LED4), .clk(CLK));  // open: clr
  and and_1 (and_1_out, WE, LEDCS);
  Decoder #(.select(4)) decoder_1 (
    .out0(LED0END), .out1(LED1END), .out2(LED2END), .out3(LED3END), .out4(LED4END), .out5(LED5END),
    .out6(LED6END), .out7(LED7END), .out8(LED8END), .out9(LED9END), .out10(LEDAEND), .out11(LEDBEND),
    .out12(LEDCEND), .out13(LEDDEND), .out14(LEDEEND), .out15(LEDFEND), .sel(ADDR[3:0]), .en(and_1_out));
  Register #(.width(15)) register_6 (.D(DATAL5), .en(LED5EN), .Q(LED5), .clk(CLK));  // open: clr
  Register #(.width(15)) register_7 (.D(DATAL6), .en(LED6EN), .Q(LED6), .clk(CLK));  // open: clr
  Register #(.width(15)) register_8 (.D(DATAL7), .en(LED7EN), .Q(LED7), .clk(CLK));  // open: clr
  Register #(.width(15)) register_9 (.D(DATAL8), .en(LED8EN), .Q(LED8), .clk(CLK));  // open: clr
  Register #(.width(15)) register_10 (.D(DATAL9), .en(LED9EN), .Q(LED9), .clk(CLK));  // open: clr
  or or_1 (LED0EN, LED0END, LEDFEND);
  or or_2 (LED1EN, LED1END, LEDFEND);
  or or_3 (LED2EN, LED2END, LEDFEND);
  or or_4 (LED3EN, LED3END, LEDFEND);
  or or_5 (LED4EN, LED4END, LEDFEND);
  or or_6 (LED5EN, LED5END, LEDFEND);
  or or_7 (LED6EN, LED6END, LEDFEND);
  or or_8 (LED7EN, LED7END, LEDFEND);
  or or_9 (LED8EN, LED8END, LEDFEND);
  or or_10 (LED9EN, LED9END, LEDFEND);
  or or_11 (LEDAEN, LEDAEND, LEDFEND);
  or or_12 (LEDBEN, LEDBEND, LEDFEND);
  or or_13 (LEDCEN, LEDCEND, LEDFEND);
  or or_14 (LEDDEN, LEDDEND, LEDFEND);
  or or_15 (LEDEEN, LEDEEND, LEDFEND);
  Pull_Resistor pull_resistor_1 (.node(KBDATA15[14]));
  Pull_Resistor pull_resistor_2 (.node(KBDATA15[13]));
  Pull_Resistor pull_resistor_3 (.node(KBDATA15[12]));
  Pull_Resistor pull_resistor_4 (.node(KBDATA15[11]));
  Pull_Resistor pull_resistor_5 (.node(KBDATA15[10]));
  Pull_Resistor pull_resistor_6 (.node(KBDATA15[9]));
  Pull_Resistor pull_resistor_7 (.node(KBDATA15[8]));
  Pull_Resistor pull_resistor_8 (.node(DATA7));
  Register #(.width(15)) register_11 (.D(DATALA), .en(LEDAEN), .Q(LEDA), .clk(CLK));  // open: clr
  Register #(.width(15)) register_12 (.D(DATALB), .en(LEDBEN), .Q(LEDB), .clk(CLK));  // open: clr
  Register #(.width(15)) register_13 (.D(DATALC), .en(LEDCEN), .Q(LEDC), .clk(CLK));  // open: clr
  Register #(.width(15)) register_14 (.D(DATALD), .en(LEDDEN), .Q(LEDD), .clk(CLK));  // open: clr
  Register #(.width(15)) register_15 (.D(DATALE), .en(LEDEEN), .Q(LEDE), .clk(CLK));  // open: clr
  Multiplexer #(.width(15)) multiplexer_1 (.in0(CPUDATAIN), .in1(LED1), .out(DATAL0), .sel(LEDFEND));
  Multiplexer #(.width(15)) multiplexer_2 (.in0(CPUDATAIN), .in1(LED2), .out(DATAL1), .sel(LEDFEND));
  Multiplexer #(.width(15)) multiplexer_3 (.in0(CPUDATAIN), .in1(LED3), .out(DATAL2), .sel(LEDFEND));
  Multiplexer #(.width(15)) multiplexer_4 (.in0(CPUDATAIN), .in1(LED4), .out(DATAL3), .sel(LEDFEND));
  Multiplexer #(.width(15)) multiplexer_5 (.in0(CPUDATAIN), .in1(LED5), .out(DATAL4), .sel(LEDFEND));
  Multiplexer #(.select(4), .width(15)) multiplexer_6 (
    .in0(LED0), .in1(LED1), .in2(LED2), .in3(LED3), .in4(LED4), .in5(LED5), .in6(LED6), .in7(LED7),
    .in8(LED8), .in9(LED9), .in10(LEDA), .in11(LEDB), .in12(LEDC), .in13(LEDD), .in14(LEDE),
    .in15({15{1'b0}}), .out(LEDDATA), .sel(ADDR[3:0]));
  Multiplexer #(.width(15)) multiplexer_7 (.in0(CPUDATAIN), .in1(LED6), .out(DATAL5), .sel(LEDFEND));
  Multiplexer #(.width(15)) multiplexer_8 (.in0(CPUDATAIN), .in1(LED7), .out(DATAL6), .sel(LEDFEND));
  Multiplexer #(.width(15)) multiplexer_9 (.in0(CPUDATAIN), .in1(LED8), .out(DATAL7), .sel(LEDFEND));
  Multiplexer #(.width(15)) multiplexer_10 (.in0(CPUDATAIN), .in1(LED9), .out(DATAL8), .sel(LEDFEND));
  Multiplexer #(.width(15)) multiplexer_11 (.in0(CPUDATAIN), .in1(LEDA), .out(DATAL9), .sel(LEDFEND));
  and and_2 (LEDRE, RE, LEDCS);
  Multiplexer #(.width(15)) multiplexer_12 (.in0(CPUDATAIN), .in1(LEDB), .out(DATALA), .sel(LEDFEND));
  Multiplexer #(.width(15)) multiplexer_13 (.in0(CPUDATAIN), .in1(LEDC), .out(DATALB), .sel(LEDFEND));
  Multiplexer #(.width(15)) multiplexer_14 (.in0(CPUDATAIN), .in1(LEDD), .out(DATALC), .sel(LEDFEND));
  Multiplexer #(.width(15)) multiplexer_15 (.in0(CPUDATAIN), .in1(LEDE), .out(DATALD), .sel(LEDFEND));
  Multiplexer #(.width(15)) multiplexer_16 (.in0(CPUDATAIN), .in1(CPUDATAIN), .out(DATALE), .sel(LEDFEND));
  and and_3 (IOCS, ADDR[5], ADDR[6], ADDR[7], ADDR[8], ADDR[9], ADDR[10], ADDR[11], ADDR[12], ADDR[13], ADDR[14], 1'b1);
  and and_4 (TTYCS, IOCS, ADDR[0], ~ADDR[1], ~ADDR[2], ~ADDR[3], ADDR[4]);  // AND_Gate
  and and_5 (KBCS, IOCS, ~ADDR[0], ~ADDR[1], ~ADDR[2], ~ADDR[3], ADDR[4]);  // AND_Gate
  and and_6 (IVECTADDR, ADDR[0], ADDR[1], ADDR[2], ADDR[3], ADDR[4], ADDR[5], ADDR[6], ADDR[7], ADDR[8], ADDR[9], ADDR[10], ADDR[11], ADDR[12], ADDR[13], ADDR[14]);
  and and_7 (TTYWR, TTYCS, WE);
  and and_8 (and_8_out, TTYWR, DATA7);
  and and_9 (KBRD, KBCS, RE);
  and and_10 (and_10_out, KBCS, WE);
  Multiplexer multiplexer_17 (.in0(and_10_out), .in1(1'b0), .out(multiplexer_17_out), .sel(KBCLR));
  and and_11 (LEDCS, IOCS, ~ADDR[4], RWE);  // AND_Gate
  and and_12 (IVECTEN, IVECTADDR, WE);
  and and_13 (IVECTRE, IVECTADDR, RE);
  or or_16 (RWE, RE, WE);
  and and_14 (MEMCS, ~IOCS, RWE);  // AND_Gate
  Multiplexer multiplexer_18 (.in0(and_8_out), .in1(1'b0), .out(multiplexer_18_out), .sel(TTYCLR));
  D_Flip_Flop d_ff_1 (.clk(CLK), .D(multiplexer_17_out), .Q(KBCLR));  // open: Qn, preset, reset
  Register #(.width(15)) register_16 (.D(CPUDATAIN), .en(IVECTEN), .Q(IVECT), .clk(CLK));  // open: clr
  D_Flip_Flop d_ff_2 (.clk(CLK), .D(multiplexer_18_out), .Q(TTYCLR));  // open: Qn, preset, reset

  assign IRQ = KBIRQ;
  assign TTYDATA = CPUDATAIN[6:0];

  // Other names for the same wires on the sheet: DATA[14:0] = CPUDATAIN; KBDATA15[7:0] = {DATA7, KBDATA}
endmodule

module ADDER15 (
  input  [14:0] A,
  input  [14:0] B,
  input  CIN,
  output COUT,
  output [14:0] S
);

  wire cla_1_cout, cla_2_cout;

  CLA cla_1 (.A(A[4:0]), .B(B[4:0]), .CIN(CIN), .COUT(cla_1_cout), .S(S[4:0]));
  CLA cla_2 (.A(A[9:5]), .B(B[9:5]), .CIN(cla_1_cout), .COUT(cla_2_cout), .S(S[9:5]));
  CLA cla_3 (.A(A[14:10]), .B(B[14:10]), .CIN(cla_2_cout), .COUT(COUT), .S(S[14:10]));
endmodule

module REGS15 (
  input  [14:0] D,
  input  W,
  input  [2:0] SelD,
  input  CLK,
  input  [2:0] SelA,
  input  [2:0] SelB,
  output [14:0] R0,
  output [14:0] R1,
  output [14:0] R2,
  output [14:0] R3,
  output [14:0] R4,
  output [14:0] R5,
  output [14:0] R6,
  output [14:0] R7,
  output [14:0] A,
  output [14:0] B
);

  wire R0write, R1write, R2write, R3write, R4write, R5write, R6write, R7write;

  Register #(.width(15)) register_1 (.D(D), .en(R0write), .clk(CLK), .Q(R0));  // open: clr
  Register #(.width(15)) register_2 (.D(D), .en(R2write), .clk(CLK), .Q(R2));  // open: clr
  Register #(.width(15)) register_3 (.D(D), .en(R4write), .clk(CLK), .Q(R4));  // open: clr
  Register #(.width(15)) register_4 (.D(D), .en(R6write), .clk(CLK), .Q(R6));  // open: clr
  Register #(.width(15)) register_5 (.D(D), .en(R3write), .clk(CLK), .Q(R3));  // open: clr
  Register #(.width(15)) register_6 (.D(D), .en(R1write), .clk(CLK), .Q(R1));  // open: clr
  Register #(.width(15)) register_7 (.D(D), .en(R5write), .clk(CLK), .Q(R5));  // open: clr
  Register #(.width(15)) register_8 (.D(D), .en(R7write), .clk(CLK), .Q(R7));  // open: clr
  Demultiplexer #(.select(3)) demultiplexer_1 (
    .out0(R0write), .out1(R1write), .out2(R2write), .out3(R3write), .out4(R4write), .out5(R5write),
    .out6(R6write), .out7(R7write), .in(W), .sel(SelD));
  Multiplexer #(.select(3), .width(15)) multiplexer_1 (
    .in0(R0), .in1(R1), .in2(R2), .in3(R3), .in4(R4), .in5(R5), .in6(R6), .in7(R7), .out(A), .sel(SelA));
  Multiplexer #(.select(3), .width(15)) multiplexer_2 (
    .in0(R0), .in1(R1), .in2(R2), .in3(R3), .in4(R4), .in5(R5), .in6(R6), .in7(R7), .out(B), .sel(SelB));
endmodule

module ALU15 (
  input  [14:0] A,
  input  [14:0] B,
  input  [2:0] OP,
  input  CIN,
  input  OIN,
  output C,
  output O,
  output N,
  output Z,
  output [14:0] R
);

  wire and_2_out, and_3_out, C_ADD, C_SUB, multiplexer_5_out, multiplexer_6_out, or_2_out;
  wire [14:0] ADD_RES, AND_RES, not_1_out, OR_RES, SLL_RES, SRA_RES, SRL_RES, SUB_RES, XOR_RES;

  ADDER15 adder15_1 (.A(A), .B(B), .CIN(CIN), .COUT(C_ADD), .S(ADD_RES));
  Multiplexer #(.select(3), .width(15)) multiplexer_1 (
    .in0(ADD_RES), .in1(SUB_RES), .in2(AND_RES), .in3(OR_RES), .in4(XOR_RES), .in5(SLL_RES), .in6(SRL_RES),
    .in7(SRA_RES), .out({N, R[13:0]}), .sel(OP));
  ADDER15 adder15_2 (.A(A), .B(not_1_out), .CIN(1'b1), .COUT(C_SUB), .S(SUB_RES));
  Multiplexer #(.select(4), .width(15)) multiplexer_2 (
    .in0(A), .in1({A[13:0], 1'b0}), .in2({A[12:0], 2'b00}), .in3({A[11:0], 3'b000}),
    .in4({A[10:0], 4'b0000}), .in5({A[9:0], {5{1'b0}}}), .in6({A[8:0], {6{1'b0}}}),
    .in7({A[7:0], {7{1'b0}}}), .in8({A[6:0], {8{1'b0}}}), .in9({A[5:0], {9{1'b0}}}),
    .in10({A[4:0], {10{1'b0}}}), .in11({A[3:0], {11{1'b0}}}), .in12({A[2:0], {12{1'b0}}}),
    .in13({A[1:0], {13{1'b0}}}), .in14({A[0], {14{1'b0}}}), .in15({15{1'b0}}), .out(SLL_RES), .sel(B[3:0]));
  assign not_1_out = ~B;  // NOT_Gate not_1, 15 bits wide
  assign AND_RES = A & B;  // AND_Gate and_1, 15 bits wide
  assign OR_RES = A | B;  // OR_Gate or_1, 15 bits wide
  and and_2 (and_2_out, ~A[14], ~B[14], N);  // AND_Gate
  and and_3 (and_3_out, A[14], B[14], ~N);  // AND_Gate
  or or_2 (or_2_out, and_2_out, and_3_out);
  Multiplexer #(.select(3)) multiplexer_3 (
    .in0(or_2_out), .in1(or_2_out), .in2(1'b0), .in3(1'b0), .in4(1'b0), .in5(1'b0), .in6(1'b0), .in7(1'b0),
    .out(O), .sel(OP));
  assign XOR_RES = A ^ B;  // XOR_Gate xor_1, 15 bits wide
  Multiplexer #(.select(4), .width(15)) multiplexer_4 (
    .in0(A), .in1({1'b0, A[14:1]}), .in2({2'b00, A[14:2]}), .in3({3'b000, A[14:3]}),
    .in4({4'b0000, A[14:4]}), .in5({{5{1'b0}}, A[14:5]}), .in6({{6{1'b0}}, A[14:6]}),
    .in7({{7{1'b0}}, A[14:7]}), .in8({{8{1'b0}}, A[14:8]}), .in9({{9{1'b0}}, A[14:9]}),
    .in10({{10{1'b0}}, A[14:10]}), .in11({{11{1'b0}}, A[14:11]}), .in12({{12{1'b0}}, A[14:12]}),
    .in13({{13{1'b0}}, A[14:13]}), .in14({{14{1'b0}}, A[14]}), .in15({15{1'b0}}), .out(SRL_RES), .sel(B[3:0]));
  Multiplexer #(.select(4)) multiplexer_5 (
    .in0(1'b0), .in1(A[14]), .in2(A[13]), .in3(A[12]), .in4(A[11]), .in5(A[10]), .in6(A[9]), .in7(A[8]),
    .in8(A[7]), .in9(A[6]), .in10(A[5]), .in11(A[4]), .in12(A[3]), .in13(A[2]), .in14(A[1]), .in15(A[0]),
    .out(multiplexer_5_out), .sel(B[3:0]));
  Multiplexer #(.select(4)) multiplexer_6 (
    .in0(1'b0), .in1(A[0]), .in2(A[1]), .in3(A[2]), .in4(A[3]), .in5(A[4]), .in6(A[5]), .in7(A[6]),
    .in8(A[7]), .in9(A[8]), .in10(A[9]), .in11(A[10]), .in12(A[11]), .in13(A[12]), .in14(A[13]),
    .in15(A[14]), .out(multiplexer_6_out), .sel(B[3:0]));
  nor nor_1 (Z, R[0], R[1], R[2], R[3], R[4], R[5], R[6], R[7], R[8], R[9], R[10], R[11], R[12], R[13], N);
  Multiplexer #(.select(3)) multiplexer_7 (
    .in0(C_ADD), .in1(C_SUB), .in2(1'b0), .in3(1'b0), .in4(1'b0), .in5(multiplexer_5_out),
    .in6(multiplexer_6_out), .in7(multiplexer_6_out), .out(C), .sel(OP));
  Multiplexer #(.select(4), .width(15)) multiplexer_8 (
    .in0(A), .in1({{2{A[14]}}, A[13:1]}), .in2({{3{A[14]}}, A[13:2]}), .in3({{4{A[14]}}, A[13:3]}),
    .in4({{5{A[14]}}, A[13:4]}), .in5({{6{A[14]}}, A[13:5]}), .in6({{7{A[14]}}, A[13:6]}),
    .in7({{8{A[14]}}, A[13:7]}), .in8({{9{A[14]}}, A[13:8]}), .in9({{10{A[14]}}, A[13:9]}),
    .in10({{11{A[14]}}, A[13:10]}), .in11({{12{A[14]}}, A[13:11]}), .in12({{13{A[14]}}, A[13:12]}),
    .in13({{14{A[14]}}, A[13]}), .in14({15{A[14]}}), .in15({15{A[14]}}), .out(SRA_RES), .sel(B[3:0]));

  assign R[14] = N;
endmodule

module FLAGS8 (
  input  IRQ,
  input  [7:0] NF,
  input  [7:0] WM,
  input  CLK,
  output [7:0] F
);

  wire [7:0] register_1_q, register_2_q;

  Register register_1 (.D(WM), .clk(CLK), .Q(register_1_q));  // open: en, clr
  Register register_2 (.D(NF), .clk(CLK), .Q(register_2_q));  // open: en, clr
  Multiplexer #(.width(8)) multiplexer_1 (.in0(register_2_q), .in1(register_1_q), .out(F), .sel(IRQ));
endmodule

module IMM15 (
  input  [14:0] INST,
  output [14:0] SEXT
);

  wire [11:0] bit_extender_4_out;
  wire [14:0] bit_extender_1_out, bit_extender_2_out, bit_extender_3_out, bit_extender_5_out;

  assign bit_extender_1_out = {{11{INST[14]}}, INST[14:11]};  // Bit_Extender bit_extender_1
  assign bit_extender_2_out = {{5{INST[9]}}, INST[9:0]};  // Bit_Extender bit_extender_2
  assign bit_extender_3_out = {{8{INST[6]}}, INST[6:0]};  // Bit_Extender bit_extender_3
  assign bit_extender_4_out = {{11{INST[14]}}, INST[14]};  // Bit_Extender bit_extender_4
  assign bit_extender_5_out = {{8{INST[10]}}, INST[10:4]};  // Bit_Extender bit_extender_5
  Multiplexer #(.select(5), .width(15)) multiplexer_1 (
    .in0({15{1'b0}}), .in1({15{1'b0}}), .in2({15{1'b0}}), .in3({15{1'b0}}), .in4({15{1'b0}}),
    .in5({15{1'b0}}), .in6({15{1'b0}}), .in7({15{1'b0}}), .in8(bit_extender_1_out), .in9(bit_extender_1_out),
    .in10(bit_extender_1_out), .in11(bit_extender_1_out), .in12(bit_extender_1_out),
    .in13(bit_extender_1_out), .in14(bit_extender_1_out), .in15(bit_extender_1_out),
    .in16(bit_extender_2_out), .in17(bit_extender_2_out), .in18(bit_extender_2_out),
    .in19(bit_extender_2_out), .in20(bit_extender_2_out), .in21(bit_extender_2_out), .in22({15{1'b0}}),
    .in23({15{1'b0}}), .in24({15{1'b0}}), .in25({15{1'b0}}), .in26({15{1'b0}}), .in27(bit_extender_1_out),
    .in28(bit_extender_3_out), .in29(bit_extender_3_out), .in30({bit_extender_4_out, INST[2:0]}),
    .in31(bit_extender_5_out), .out(SEXT), .sel(INST[4:0]));
endmodule

module DECODE15 (
  input  [4:0] OPCODE,
  output SWI,
  output STORE,
  output LOAD,
  output [1:0] ASEL,
  output [1:0] BSEL,
  output [2:0] ALUOP,
  output [2:0] REGDATASRC,
  output REGW,
  output [1:0] FLAGSRC,
  output [7:0] FLAGWM,
  output SRPW,
  output SRFW
);

  ROM #(.addrWidth(5), .dataWidth(23)) rom_1 (
    .addr(OPCODE), .data({ASEL, BSEL, ALUOP, REGDATASRC, REGW, FLAGSRC, FLAGWM, SRPW, SRFW}));
  and and_1 (SWI, OPCODE[0], OPCODE[1], OPCODE[2], ~OPCODE[3], OPCODE[4]);  // AND_Gate
  and and_2 (STORE, ~OPCODE[0], OPCODE[1], OPCODE[2], OPCODE[3], OPCODE[4]);  // AND_Gate
  and and_3 (LOAD, OPCODE[0], ~OPCODE[1], ~OPCODE[2], OPCODE[3], ~OPCODE[4]);  // AND_Gate

  // Notes on the sheet:
  //   ASEL/BSEL : 00- Register as source
  //   01- Immediate as source
  //   10- PC as source
  //   11- Memory as source
  //   contents of rom_1 (hex, n*v repeats v):
  //   143c 1143c 2140c 3140c 4140c 5140c 6140c 7140c 8143c 83000 a140c b140c c140c d140c e140c f140c
  //   6*80000 80003 80d83 143e 143d 143d 487002 487002 487001 80000 8143c
  //   FLAGSRC : 00- No update
  //   01- Update based on ALU result
  //   10- Update based on immediate
  //   11- Update based on interrupt
  //   REGDATASRC : 000- ALU result
  //   001- Memory data
  //   011- PC
endmodule

module CLA (
  input  [4:0] A,
  input  [4:0] B,
  input  CIN,
  output COUT,
  output [4:0] S
);

  wire and_1_out, and_2_out, and_3_out, and_4_out, and_5_out, and_6_out, and_7_out, and_8_out, and_9_out,
       and_10_out, and_11_out, and_12_out, and_13_out, C1_out, C2_out, c3_out, c4_out, g0_out, g1_out,
       g2_out, g3_out, g4_out, P0_out, p1_out, p2_out, p3_out, p4_out, pc0_out, pc1_out;

  and g1 (g1_out, B[1], A[1]);
  xor p2 (p2_out, A[2], B[2]);
  and g2 (g2_out, B[2], A[2]);
  xor p3 (p3_out, A[3], B[3]);
  and g3 (g3_out, A[3], B[3]);
  xor p4 (p4_out, A[4], B[4]);
  and g4 (g4_out, A[4], B[4]);
  xor P0 (P0_out, A[0], B[0]);
  and g0 (g0_out, B[0], A[0]);
  xor p1 (p1_out, A[1], B[1]);
  and pc0 (pc0_out, CIN, P0_out);
  and pc1 (pc1_out, C1_out, P0_out, p1_out);
  and and_1 (and_1_out, p1_out, g0_out);
  and and_2 (and_2_out, g1_out, p2_out);
  and and_3 (and_3_out, p2_out, p1_out, g0_out);
  and and_4 (and_4_out, p2_out, p1_out, P0_out, C2_out);
  xor xor_1 (S[0], P0_out, CIN);
  xor xor_2 (S[1], p1_out, C1_out);
  xor xor_3 (S[2], p2_out, C2_out);
  xor xor_4 (S[3], p3_out, c3_out);
  and and_5 (and_5_out, g2_out, p3_out);
  and and_6 (and_6_out, p3_out, p2_out, g1_out);
  and and_7 (and_7_out, p3_out, p2_out, p1_out, g0_out);
  and and_8 (and_8_out, p3_out, p2_out, p1_out, P0_out, c3_out);
  and and_9 (and_9_out, p4_out, g3_out);
  and and_10 (and_10_out, p4_out, p3_out, g2_out);
  and and_11 (and_11_out, p4_out, p3_out, p2_out, g1_out);
  and and_12 (and_12_out, p4_out, p3_out, p2_out, p1_out, g0_out);
  and and_13 (and_13_out, p4_out, p3_out, p2_out, p1_out, P0_out, c4_out);
  or C1 (C1_out, pc0_out, g0_out);
  or C2 (C2_out, pc1_out, g1_out, and_1_out);
  or c3 (c3_out, and_3_out, and_2_out, g2_out, and_4_out);
  or c4 (c4_out, g3_out, and_5_out, and_6_out, and_7_out, and_8_out);
  xor xor_5 (S[4], p4_out, c4_out);
  or c5 (COUT, g4_out, and_9_out, and_10_out, and_11_out, and_12_out, and_13_out);
endmodule
